// Digital circuit adding_machine.dig as structural Verilog
module adding_machine (
  input  [7:0] A,
  input  [7:0] B,
  input  in_3,
  input  V,
  input  V_2,
  output [7:0] out_4
);

  wire _8_Bit_Adder_co, not_1_out;
  wire [7:0] _8_Bit_2_to1_Selector_out, _8_Bit_Latch__8;

  not not_1 (not_1_out, V_2);
  _8_bit_latch_simple _8_Bit_Latch (.D(out_4), .Clock(not_1_out), ._8(_8_Bit_Latch__8));
  _8_bit_2_to_1_selector _8_Bit_2_to1_Selector (
    .A(B), .B(_8_Bit_Latch__8), .Select(V), .Out(_8_Bit_2_to1_Selector_out));
  eight_bit_adder _8_Bit_Adder (.A(A), .B(_8_Bit_2_to1_Selector_out), .Ci(in_3), .Co(_8_Bit_Adder_co), .D(out_4));
  LED Co (.in(_8_Bit_Adder_co));
endmodule
